// Logisim project 8-bit CPU.circ as structural Verilog: 2 circuits, main circuit ALU
module ALU (
  input  B7,
  input  B6,
  input  B5,
  input  B4,
  input  B3,
  input  B2,
  input  B1,
  input  B0,
  input  A7,
  input  A6,
  input  A5,
  input  A4,
  input  A3,
  input  A2,
  input  A1,
  input  A0,
  input  ENB,
  input  ENA,
  input  INVA,
  input  Carry_In,
  input  F1,
  input  F0,
  input  Clk,
  output Carry_Out,
  output C7,
  output C6,
  output C5,
  output C4,
  output C3,
  output C2,
  output C1,
  output C0
);

  wire n2_to_4_decoder_1_a___b, n2_to_4_decoder_1_a___nb, n2_to_4_decoder_1_na___b,
       n2_to_4_decoder_1_na___nb, not_1_out, not_2_out, not_3_out;
  wire [7:0] controlled_buffer_1_out, controlled_buffer_5_out, controlled_buffer_7_out,
       n8_bit_bitwise_and_1__07, n8_bit_bitwise_not_1__07, n8_bit_bitwise_or_1__07, n8bitripplecarryadder_1_s;

  assign controlled_buffer_1_out = not_1_out ? {8{ENB}} : 8'bz;  // Controlled_Buffer controlled_buffer_1
  not not_1 (not_1_out, ENB);
  not not_2 (not_2_out, ENA);
  assign controlled_buffer_1_out = ENB ? {B7, B6, B5, B4, B3, B2, B1, B0} : 8'bz;  // Controlled_Buffer controlled_buffer_2
  _2_to_4_Decoder u_2_to_4_decoder_1 (
    .A(F1), .B(F0), .Enable(Clk), .nA___nB(n2_to_4_decoder_1_na___nb), .A___nB(n2_to_4_decoder_1_a___nb),
    .nA___B(n2_to_4_decoder_1_na___b), .A___B(n2_to_4_decoder_1_a___b));
  _8_bit_Bitwise_AND u_8_bit_bitwise_and_1 (
    .A7(controlled_buffer_7_out[0]), .A6(controlled_buffer_7_out[1]), .A5(controlled_buffer_7_out[2]),
    .A4(controlled_buffer_7_out[3]), .A3(controlled_buffer_7_out[4]), .A2(controlled_buffer_7_out[5]),
    .A1(controlled_buffer_7_out[6]), .A0(controlled_buffer_7_out[7]), .B7(controlled_buffer_1_out[0]),
    .B6(controlled_buffer_1_out[1]), .B5(controlled_buffer_1_out[2]), .B4(controlled_buffer_1_out[3]),
    .B3(controlled_buffer_1_out[4]), .B2(controlled_buffer_1_out[5]), .B1(controlled_buffer_1_out[6]),
    .B0(controlled_buffer_1_out[7]), ._07(n8_bit_bitwise_and_1__07[0]), ._06(n8_bit_bitwise_and_1__07[1]),
    ._05(n8_bit_bitwise_and_1__07[2]), ._04(n8_bit_bitwise_and_1__07[3]), ._03(n8_bit_bitwise_and_1__07[4]),
    ._02(n8_bit_bitwise_and_1__07[5]), ._01(n8_bit_bitwise_and_1__07[6]), ._00(n8_bit_bitwise_and_1__07[7]));
  assign {C7, C6, C5, C4, C3, C2, C1, C0} = n2_to_4_decoder_1_na___nb ? n8_bit_bitwise_and_1__07 : 8'bz;  // Controlled_Buffer controlled_buffer_3
  _8_bit_Bitwise_OR u_8_bit_bitwise_or_1 (
    .A7(controlled_buffer_7_out[0]), .A6(controlled_buffer_7_out[1]), .A5(controlled_buffer_7_out[2]),
    .A4(controlled_buffer_7_out[3]), .A3(controlled_buffer_7_out[4]), .A2(controlled_buffer_7_out[5]),
    .A1(controlled_buffer_7_out[6]), .A0(controlled_buffer_7_out[7]), .B7(controlled_buffer_1_out[0]),
    .B6(controlled_buffer_1_out[1]), .B5(controlled_buffer_1_out[2]), .B4(controlled_buffer_1_out[3]),
    .B3(controlled_buffer_1_out[4]), .B2(controlled_buffer_1_out[5]), .B1(controlled_buffer_1_out[6]),
    .B0(controlled_buffer_1_out[7]), ._07(n8_bit_bitwise_or_1__07[0]), ._06(n8_bit_bitwise_or_1__07[1]),
    ._05(n8_bit_bitwise_or_1__07[2]), ._04(n8_bit_bitwise_or_1__07[3]), ._03(n8_bit_bitwise_or_1__07[4]),
    ._02(n8_bit_bitwise_or_1__07[5]), ._01(n8_bit_bitwise_or_1__07[6]), ._00(n8_bit_bitwise_or_1__07[7]));
  assign {C7, C6, C5, C4, C3, C2, C1, C0} = n2_to_4_decoder_1_a___nb ? n8_bit_bitwise_or_1__07 : 8'bz;  // Controlled_Buffer controlled_buffer_4
  assign controlled_buffer_5_out = not_2_out ? {8{ENA}} : 8'bz;  // Controlled_Buffer controlled_buffer_5
  not not_3 (not_3_out, INVA);
  _8bitRippleCarryAdder u_8bitripplecarryadder_1 (
    .Cout(Carry_Out), .Cin(Carry_In), .A(controlled_buffer_7_out), .B(controlled_buffer_1_out),
    .S(n8bitripplecarryadder_1_s));
  assign controlled_buffer_5_out = ENA ? {A7, A6, A5, A4, A3, A2, A1, A0} : 8'bz;  // Controlled_Buffer controlled_buffer_6
  assign controlled_buffer_7_out = not_3_out ? controlled_buffer_5_out : 8'bz;  // Controlled_Buffer controlled_buffer_7
  _8_bit_Bitwise_NOT u_8_bit_bitwise_not_1 (
    .A7(controlled_buffer_1_out[0]), .A6(controlled_buffer_1_out[1]), .A5(controlled_buffer_1_out[2]),
    .A4(controlled_buffer_1_out[3]), .A3(controlled_buffer_1_out[4]), .A2(controlled_buffer_1_out[5]),
    .A1(controlled_buffer_1_out[6]), .A0(controlled_buffer_1_out[7]), ._07(n8_bit_bitwise_not_1__07[0]),
    ._06(n8_bit_bitwise_not_1__07[1]), ._05(n8_bit_bitwise_not_1__07[2]), ._04(n8_bit_bitwise_not_1__07[3]),
    ._03(n8_bit_bitwise_not_1__07[4]), ._02(n8_bit_bitwise_not_1__07[5]), ._01(n8_bit_bitwise_not_1__07[6]),
    ._00(n8_bit_bitwise_not_1__07[7]));
  assign {C7, C6, C5, C4, C3, C2, C1, C0} = n2_to_4_decoder_1_na___b ? n8_bit_bitwise_not_1__07 : 8'bz;  // Controlled_Buffer controlled_buffer_8
  assign controlled_buffer_7_out = INVA ? ~controlled_buffer_5_out : 8'bz;  // Controlled_Inverter controlled_inverter_1
  assign {C7, C6, C5, C4, C3, C2, C1, C0} = n2_to_4_decoder_1_a___b ? n8bitripplecarryadder_1_s : 8'bz;  // Controlled_Buffer controlled_buffer_9
endmodule

module CPU (
  input  [7:0] In_From_Data_Bus,
  input  CLk,
  input  Fetch,
  input  MAR,
  input  MDR,
  input  PC,
  input  MBR,
  input  SP,
  input  LV,
  input  CCP,
  input  TOS,
  input  OPC,
  input  H,
  input  ENB,
  input  ENA,
  input  INVA,
  input  Inc,
  input  F1,
  input  F0,
  input  LRS,
  input  ENS,
  input  [2:0] B_Bus,
  output [7:0] To_Address_Bus,
  output [7:0] To_Data_Bus,
  output Carry_Out_Flag_Register
);

  wire and_1_out, and_2_out, and_3_out, and_4_out, and_5_out, and_6_out, and_7_out, and_8_out, and_9_out,
       and_10_out, decoder_1_out0, decoder_1_out1, decoder_1_out2, decoder_1_out3, decoder_1_out4,
       decoder_1_out5, decoder_1_out6, decoder_1_out7, not_1_out, not_2_out;
  wire [7:0] alu_1_c0, controlled_buffer_1_out, controlled_buffer_3_out, controlled_buffer_4_out,
       controlled_buffer_5_out, controlled_buffer_6_out, controlled_buffer_7_out, controlled_buffer_8_out,
       controlled_buffer_9_out, controlled_buffer_10_out, controlled_buffer_11_out, controlled_buffer_12_out,
       controlled_buffer_13_out, controlled_buffer_21_out, controlled_buffer_22_out, CPP_q, H_q,
       LR_Shifter_s0, LV_q, MBR_q, OPC_q, PC_q, SP_q, TOS_q;

  assign controlled_buffer_1_out = Fetch ? In_From_Data_Bus : 8'bz;  // Controlled_Buffer controlled_buffer_1
  assign controlled_buffer_1_out = not_1_out ? controlled_buffer_21_out : 8'bz;  // Controlled_Buffer controlled_buffer_2
  not not_1 (not_1_out, Fetch);
  and and_1 (and_1_out, CLk, MDR);
  and and_2 (and_2_out, CLk, MAR);
  assign controlled_buffer_3_out = and_2_out ? controlled_buffer_21_out : 8'bz;  // Controlled_Buffer controlled_buffer_3
  assign controlled_buffer_4_out = and_1_out ? controlled_buffer_1_out : 8'bz;  // Controlled_Buffer controlled_buffer_4
  and and_3 (and_3_out, CLk, MBR);
  and and_4 (and_4_out, CLk, PC);
  and and_5 (and_5_out, CLk, SP);
  assign controlled_buffer_5_out = and_4_out ? controlled_buffer_21_out : 8'bz;  // Controlled_Buffer controlled_buffer_5
  assign controlled_buffer_6_out = and_3_out ? controlled_buffer_21_out : 8'bz;  // Controlled_Buffer controlled_buffer_6
  assign controlled_buffer_7_out = and_5_out ? controlled_buffer_21_out : 8'bz;  // Controlled_Buffer controlled_buffer_7
  assign controlled_buffer_8_out = and_6_out ? controlled_buffer_21_out : 8'bz;  // Controlled_Buffer controlled_buffer_8
  assign controlled_buffer_9_out = and_7_out ? controlled_buffer_21_out : 8'bz;  // Controlled_Buffer controlled_buffer_9
  assign controlled_buffer_10_out = and_9_out ? controlled_buffer_21_out : 8'bz;  // Controlled_Buffer controlled_buffer_10
  assign controlled_buffer_11_out = and_10_out ? controlled_buffer_21_out : 8'bz;  // Controlled_Buffer controlled_buffer_11
  and and_6 (and_6_out, CLk, LV);
  and and_7 (and_7_out, CLk, CCP);
  _8_Bit_Register u_MAR (.CLK(and_2_out), .D(controlled_buffer_3_out), .Q(To_Address_Bus));
  _8_Bit_Register u_MDR (.CLK(and_1_out), .D(controlled_buffer_4_out), .Q(To_Data_Bus));
  _8_Bit_Register u_PC (.CLK(and_4_out), .D(controlled_buffer_5_out), .Q(PC_q));
  _8_Bit_Register u_MBR (.CLK(and_3_out), .D(controlled_buffer_6_out), .Q(MBR_q));
  _8_Bit_Register u_SP (.CLK(and_5_out), .D(controlled_buffer_7_out), .Q(SP_q));
  _8_Bit_Register u_LV (.CLK(and_6_out), .D(controlled_buffer_8_out), .Q(LV_q));
  _8_Bit_Register CPP (.CLK(and_7_out), .D(controlled_buffer_9_out), .Q(CPP_q));
  _8_Bit_Register u_TOS (.CLK(and_9_out), .D(controlled_buffer_10_out), .Q(TOS_q));
  _8_Bit_Register u_OPC (.CLK(and_10_out), .D(controlled_buffer_11_out), .Q(OPC_q));
  assign controlled_buffer_12_out = and_8_out ? controlled_buffer_21_out : 8'bz;  // Controlled_Buffer controlled_buffer_12
  _8_Bit_Register u_H (.CLK(and_8_out), .D(controlled_buffer_12_out), .Q(H_q));
  and and_8 (and_8_out, CLk, H);
  and and_9 (and_9_out, CLk, TOS);
  and and_10 (and_10_out, CLk, OPC);
  assign controlled_buffer_13_out = decoder_1_out0 ? To_Data_Bus : 8'bz;  // Controlled_Buffer controlled_buffer_13
  assign controlled_buffer_13_out = decoder_1_out1 ? PC_q : 8'bz;  // Controlled_Buffer controlled_buffer_14
  assign controlled_buffer_13_out = decoder_1_out2 ? MBR_q : 8'bz;  // Controlled_Buffer controlled_buffer_15
  assign controlled_buffer_13_out = decoder_1_out3 ? SP_q : 8'bz;  // Controlled_Buffer controlled_buffer_16
  assign controlled_buffer_13_out = decoder_1_out4 ? LV_q : 8'bz;  // Controlled_Buffer controlled_buffer_17
  assign controlled_buffer_13_out = decoder_1_out5 ? CPP_q : 8'bz;  // Controlled_Buffer controlled_buffer_18
  assign controlled_buffer_13_out = decoder_1_out6 ? TOS_q : 8'bz;  // Controlled_Buffer controlled_buffer_19
  assign controlled_buffer_13_out = decoder_1_out7 ? OPC_q : 8'bz;  // Controlled_Buffer controlled_buffer_20
  assign controlled_buffer_21_out = not_2_out ? alu_1_c0 : 8'bz;  // Controlled_Buffer controlled_buffer_21
  ALU alu_1 (
    .ENB(ENB), .ENA(ENA), .INVA(INVA), .Carry_In(Inc), .B7(controlled_buffer_13_out[7]),
    .B6(controlled_buffer_13_out[6]), .B5(controlled_buffer_13_out[5]), .B4(controlled_buffer_13_out[4]),
    .B3(controlled_buffer_13_out[3]), .B2(controlled_buffer_13_out[2]), .B1(controlled_buffer_13_out[1]),
    .B0(controlled_buffer_13_out[0]), .A7(H_q[7]), .A6(H_q[6]), .A5(H_q[5]), .A4(H_q[4]), .A3(H_q[3]),
    .A2(H_q[2]), .A1(H_q[1]), .A0(H_q[0]), .Carry_Out(Carry_Out_Flag_Register), .F1(F1), .F0(F0), .Clk(CLk),
    .C7(alu_1_c0[7]), .C6(alu_1_c0[6]), .C5(alu_1_c0[5]), .C4(alu_1_c0[4]), .C3(alu_1_c0[3]),
    .C2(alu_1_c0[2]), .C1(alu_1_c0[1]), .C0(alu_1_c0[0]));
  assign controlled_buffer_22_out = ENS ? alu_1_c0 : 8'bz;  // Controlled_Buffer controlled_buffer_22
  not not_2 (not_2_out, ENS);
  assign controlled_buffer_21_out = ENS ? LR_Shifter_s0 : 8'bz;  // Controlled_Buffer controlled_buffer_23
  _8_bit_wide_1_bit_Left_Right_Shifter LR_Shifter (
    .C(LRS), .D0(controlled_buffer_22_out[0]), .D1(controlled_buffer_22_out[1]),
    .D2(controlled_buffer_22_out[2]), .D3(controlled_buffer_22_out[3]), .D4(controlled_buffer_22_out[4]),
    .D5(controlled_buffer_22_out[5]), .D6(controlled_buffer_22_out[6]), .D7(controlled_buffer_22_out[7]),
    .S0(LR_Shifter_s0[0]), .S1(LR_Shifter_s0[1]), .S2(LR_Shifter_s0[2]), .S3(LR_Shifter_s0[3]),
    .S4(LR_Shifter_s0[4]), .S5(LR_Shifter_s0[5]), .S6(LR_Shifter_s0[6]), .S7(LR_Shifter_s0[7]));
  Decoder #(.select(3)) decoder_1 (
    .out0(decoder_1_out0), .out1(decoder_1_out1), .out2(decoder_1_out2), .out3(decoder_1_out3),
    .out4(decoder_1_out4), .out5(decoder_1_out5), .out6(decoder_1_out6), .out7(decoder_1_out7), .sel(B_Bus),
    .en(CLk));
endmodule
