// Logisim project BitwiseFunctions.circ as structural Verilog: 3 circuits, main circuit 8-bit Bitwise AND
module _8_bit_Bitwise_AND (
  input  A7,
  input  A6,
  input  A5,
  input  A4,
  input  A3,
  input  A2,
  input  A1,
  input  A0,
  input  B7,
  input  B6,
  input  B5,
  input  B4,
  input  B3,
  input  B2,
  input  B1,
  input  B0,
  output _07,
  output _06,
  output _05,
  output _04,
  output _03,
  output _02,
  output _01,
  output _00
);

  and u__07 (_07, A7, B7);
  and u__06 (_06, A6, B6);
  and u__05 (_05, A5, B5);
  and u__04 (_04, A4, B4);
  and u__03 (_03, A3, B3);
  and u__02 (_02, A2, B2);
  and u__01 (_01, A1, B1);
  and u__00 (_00, A0, B0);

  // Notes on the sheet:
  //   Input A
  //   Input B
endmodule

module _8_bit_Bitwise_OR (
  input  A7,
  input  A6,
  input  A5,
  input  A4,
  input  A3,
  input  A2,
  input  A1,
  input  A0,
  input  B7,
  input  B6,
  input  B5,
  input  B4,
  input  B3,
  input  B2,
  input  B1,
  input  B0,
  output _07,
  output _06,
  output _05,
  output _04,
  output _03,
  output _02,
  output _01,
  output _00
);

  or u__07 (_07, A7, B7);
  or u__06 (_06, A6, B6);
  or u__05 (_05, A5, B5);
  or u__04 (_04, A4, B4);
  or u__03 (_03, A3, B3);
  or u__02 (_02, A2, B2);
  or u__01 (_01, A1, B1);
  or u__00 (_00, A0, B0);

  // Notes on the sheet:
  //   Input A
  //   Input B
endmodule

module _8_bit_Bitwise_NOT (
  input  A7,
  input  A6,
  input  A5,
  input  A4,
  input  A3,
  input  A2,
  input  A1,
  input  A0,
  output _07,
  output _06,
  output _05,
  output _04,
  output _03,
  output _02,
  output _01,
  output _00
);

  not u__07 (_07, A7);
  not u__06 (_06, A6);
  not u__05 (_05, A5);
  not u__04 (_04, A4);
  not u__03 (_03, A3);
  not u__02 (_02, A2);
  not u__01 (_01, A1);
  not u__00 (_00, A0);

  // Notes on the sheet:
  //   Input A
endmodule
