// Logisim project BuildingBlocks.circ as structural Verilog: 4 circuits, main circuit 2 to 4 Decoder
module _2_to_4_Decoder (
  input  A,
  input  B,
  input  Enable,
  output nA___nB,
  output A___nB,
  output nA___B,
  output A___B
);

  wire not_1_out, not_2_out;

  not not_1 (not_1_out, A);
  not not_2 (not_2_out, B);
  and _00 (nA___nB, not_1_out, not_2_out, Enable);
  and _01 (A___nB, A, not_2_out, Enable);
  and _10 (nA___B, B, not_1_out, Enable);
  and _11 (A___B, B, A, Enable);
endmodule

module _8_to_1_MUX (
  input  D0,
  input  D1,
  input  D2,
  input  D3,
  input  D4,
  input  D5,
  input  D6,
  input  D7,
  input  A,
  input  B,
  input  C,
  output F
);

  wire _0_out, _1_out, _2_out, _3_out, _4_out, _5_out, _6_out, _7_out, not_1_out, not_2_out, not_3_out;

  not not_1 (not_1_out, B);
  not not_2 (not_2_out, A);
  not not_3 (not_3_out, C);
  and _0 (_0_out, D0, not_2_out, not_1_out, not_3_out);
  and _1 (_1_out, D1, not_2_out, not_1_out, C);
  and _2 (_2_out, D2, not_2_out, B, not_3_out);
  and _3 (_3_out, D3, not_2_out, B, C);
  and _4 (_4_out, D4, A, not_1_out, not_3_out);
  and _5 (_5_out, D5, A, not_1_out, C);
  and _6 (_6_out, D6, A, B, not_3_out);
  and _7 (_7_out, D7, A, B, C);
  or or_1 (F, _0_out, _1_out, _2_out, _3_out, _4_out, _5_out, _6_out, _7_out);
endmodule

module _8_Bit_Comparator (
  input  [7:0] A,
  input  [7:0] B,
  output X
);

  wire _0_out, _1_out, _2_out, _3_out, _4_out, _5_out, _6_out, _7_out;

  xnor _0 (_0_out, A[0], B[0]);
  xnor _1 (_1_out, A[1], B[1]);
  xnor _2 (_2_out, A[2], B[2]);
  xnor _3 (_3_out, A[3], B[3]);
  xnor _4 (_4_out, A[4], B[4]);
  xnor _5 (_5_out, A[5], B[5]);
  xnor _6 (_6_out, A[6], B[6]);
  not _7 (_7_out, A[7]);  // XNOR_Gate
  and and_1 (X, _0_out, _1_out, _2_out, _3_out, _4_out, _5_out, _6_out, _7_out);
endmodule

module _8_bit_wide_1_bit_Left_Right_Shifter (
  input  D0,
  input  D1,
  input  D2,
  input  D3,
  input  D4,
  input  D5,
  input  D6,
  input  D7,
  input  C,
  output S0,
  output S1,
  output S2,
  output S3,
  output S4,
  output S5,
  output S6,
  output S7
);

  wire and_1_out, and_3_out, and_4_out, and_5_out, and_6_out, and_7_out, and_8_out, and_9_out, and_10_out,
       and_11_out, and_12_out, and_14_out, not_1_out;

  not not_1 (not_1_out, C);
  and and_1 (and_1_out, D0, C);
  and and_2 (S0, not_1_out, D1);
  or or_1 (S1, and_1_out, and_4_out);
  and and_3 (and_3_out, D1, C);
  and and_4 (and_4_out, not_1_out, D2);
  or or_2 (S2, and_3_out, and_7_out);
  and and_5 (and_5_out, D2, C);
  and and_6 (and_6_out, D3, C);
  and and_7 (and_7_out, not_1_out, D3);
  or or_3 (S3, and_5_out, and_8_out);
  and and_8 (and_8_out, not_1_out, D4);
  and and_9 (and_9_out, D4, C);
  or or_4 (S4, and_6_out, and_10_out);
  and and_10 (and_10_out, not_1_out, D5);
  and and_11 (and_11_out, D5, C);
  or or_5 (S5, and_9_out, and_12_out);
  and and_12 (and_12_out, not_1_out, D6);
  and and_13 (S7, D6, C);
  or or_6 (S6, and_11_out, and_14_out);
  and and_14 (and_14_out, not_1_out, D7);
endmodule
