// Logisim project Latches.circ as structural Verilog: 8 circuits, main circuit SR-Latch
module SR_Latch (
  input  nS,
  input  nR,
  output Q,
  output nQ
);

  nand nand_1 (Q, nS, nQ);
  nand nand_2 (nQ, Q, nR);
endmodule

module SR_Flip_Flop (
  input  S,
  input  R,
  input  CLK,
  output Q,
  output nQ
);

  wire nand_1_out, nand_2_out;

  nand nand_1 (nand_1_out, S, CLK);
  nand nand_2 (nand_2_out, CLK, R);
  SR_Latch SR_Latch (.nS(nand_1_out), .nR(nand_2_out), .Q(Q), .nQ(nQ));
endmodule

module D_Flip_Flop (
  input  D,
  input  CLK,
  output Q,
  output nQ
);

  wire not_1_out;

  not not_1 (not_1_out, D);
  SR_Flip_Flop SR_Flip_Flop (.S(D), .R(not_1_out), .CLK(CLK), .Q(Q), .nQ(nQ));
endmodule

module _8_Bit_Register (
  input  [7:0] D,
  input  CLK,
  output [7:0] Q
);

  D_Flip_Flop _7 (.D(D[7]), .CLK(CLK), .Q(Q[7]));  // open: nQ
  D_Flip_Flop _6 (.D(D[6]), .CLK(CLK), .Q(Q[6]));  // open: nQ
  D_Flip_Flop _4 (.D(D[4]), .CLK(CLK), .Q(Q[4]));  // open: nQ
  D_Flip_Flop _5 (.D(D[5]), .CLK(CLK), .Q(Q[5]));  // open: nQ
  D_Flip_Flop _3 (.D(D[3]), .CLK(CLK), .Q(Q[3]));  // open: nQ
  D_Flip_Flop _2 (.D(D[2]), .CLK(CLK), .Q(Q[2]));  // open: nQ
  D_Flip_Flop _1 (.D(D[1]), .CLK(CLK), .Q(Q[1]));  // open: nQ
  D_Flip_Flop _0 (.D(D[0]), .CLK(CLK), .Q(Q[0]));  // open: nQ
endmodule

module Binary_Memory_Cell (
  input  Select,
  input  Data_In,
  input  Read_1_Write_0,
  output Data_Out
);

  wire and_1_out, and_2_out, not_1_out, not_2_out, R_out, S_out, SR_Latch_q;

  not not_1 (not_1_out, Data_In);
  and and_1 (and_1_out, Select, Data_In, not_2_out);
  and and_2 (and_2_out, Select, not_1_out, not_2_out);
  not not_2 (not_2_out, Read_1_Write_0);
  not S (S_out, and_1_out);
  not R (R_out, and_2_out);
  SR_Latch SR_Latch (.nS(S_out), .nR(R_out), .Q(SR_Latch_q));  // open: nQ
  and and_3 (Data_Out, Select, SR_Latch_q, Read_1_Write_0);
endmodule

module BMC_with_bi_dataBus_and_controlBus (
  input  Data_Bus_In,
  input  [1:0] Control_Bus_In,
  output Data_Bus_State,
  output [1:0] Control_Line_State
);

  wire binary_memory_cell_1_data_out, controlled_buffer_2_out, not_1_out;

  assign Data_Bus_State = not_1_out ? Data_Bus_In : 1'bz;  // Controlled_Buffer controlled_buffer_1
  not not_1 (not_1_out, Control_Bus_In[1]);
  assign controlled_buffer_2_out = not_1_out ? Data_Bus_State : 1'bz;  // Controlled_Buffer controlled_buffer_2
  Binary_Memory_Cell binary_memory_cell_1 (
    .Data_In(controlled_buffer_2_out), .Select(Control_Bus_In[0]), .Read_1_Write_0(Control_Bus_In[1]),
    .Data_Out(binary_memory_cell_1_data_out));
  assign Data_Bus_State = Control_Bus_In[1] ? binary_memory_cell_1_data_out : 1'bz;  // Controlled_Buffer controlled_buffer_3

  assign Control_Line_State = Control_Bus_In;

  // Notes on the sheet:
  //   Control Bus Lines:
  //   #0: Clock
  //   #1: Read (1) / Write (0)
endmodule

module _8_Bit_Memory_Cell (
  input  Enable,
  input  Read_1___Write_0,
  input  D0,
  input  D1,
  input  D2,
  input  D3,
  input  D4,
  input  D5,
  input  D6,
  input  D7,
  output Q0,
  output Q1,
  output Q2,
  output Q3,
  output Q4,
  output Q5,
  output Q6,
  output Q7
);

  Binary_Memory_Cell binary_memory_cell_1 (
    .Data_In(D0), .Select(Enable), .Read_1_Write_0(Read_1___Write_0), .Data_Out(Q0));
  Binary_Memory_Cell binary_memory_cell_2 (
    .Data_In(D1), .Select(Enable), .Read_1_Write_0(Read_1___Write_0), .Data_Out(Q1));
  Binary_Memory_Cell binary_memory_cell_3 (
    .Data_In(D2), .Select(Enable), .Read_1_Write_0(Read_1___Write_0), .Data_Out(Q2));
  Binary_Memory_Cell binary_memory_cell_4 (
    .Data_In(D3), .Select(Enable), .Read_1_Write_0(Read_1___Write_0), .Data_Out(Q3));
  Binary_Memory_Cell binary_memory_cell_5 (
    .Data_In(D4), .Select(Enable), .Read_1_Write_0(Read_1___Write_0), .Data_Out(Q4));
  Binary_Memory_Cell binary_memory_cell_6 (
    .Data_In(D5), .Select(Enable), .Read_1_Write_0(Read_1___Write_0), .Data_Out(Q5));
  Binary_Memory_Cell binary_memory_cell_7 (
    .Data_In(D6), .Select(Enable), .Read_1_Write_0(Read_1___Write_0), .Data_Out(Q6));
  Binary_Memory_Cell binary_memory_cell_8 (
    .Data_In(D7), .Select(Enable), .Read_1_Write_0(Read_1___Write_0), .Data_Out(Q7));
endmodule

module _4_Byte_Memory_Chip (
  input  [7:0] in_1,
  input  [7:0] in_2,
  input  [1:0] in_3,
  output [7:0] _8_Bit_Data_Bus,
  output [7:0] _8_Bit_Address_Buss,
  output [1:0] Control_Bus
);

  wire and_1_out, Chip_Select_Address_out, n2_to_4_decoder_1_a___b, n2_to_4_decoder_1_a___nb,
       n2_to_4_decoder_1_na___b, n2_to_4_decoder_1_na___nb, n8_bit_memory_cell_1_q0, n8_bit_memory_cell_1_q1,
       n8_bit_memory_cell_1_q2, n8_bit_memory_cell_1_q3, n8_bit_memory_cell_1_q4, n8_bit_memory_cell_1_q5,
       n8_bit_memory_cell_1_q6, n8_bit_memory_cell_1_q7, n8_bit_memory_cell_2_q0, n8_bit_memory_cell_2_q1,
       n8_bit_memory_cell_2_q2, n8_bit_memory_cell_2_q3, n8_bit_memory_cell_2_q4, n8_bit_memory_cell_2_q5,
       n8_bit_memory_cell_2_q6, n8_bit_memory_cell_2_q7, n8_bit_memory_cell_3_q0, n8_bit_memory_cell_3_q1,
       n8_bit_memory_cell_3_q2, n8_bit_memory_cell_3_q3, n8_bit_memory_cell_3_q4, n8_bit_memory_cell_3_q5,
       n8_bit_memory_cell_3_q6, n8_bit_memory_cell_3_q7, n8_bit_memory_cell_4_q0, n8_bit_memory_cell_4_q1,
       n8_bit_memory_cell_4_q2, n8_bit_memory_cell_4_q3, n8_bit_memory_cell_4_q4, n8_bit_memory_cell_4_q5,
       n8_bit_memory_cell_4_q6, n8_bit_memory_cell_4_q7, not_1_out, not_2_out, or_1_out;
  wire [7:0] controlled_buffer_2_out, D0_out;

  and Chip_Select_Address (Chip_Select_Address_out, not_1_out, in_3[0]);
  not not_1 (not_1_out, or_1_out);
  and and_1 (and_1_out, in_3[1], in_3[0]);
  _2_to_4_Decoder u_2_to_4_decoder_1 (
    .A(in_2[1]), .B(in_2[0]), .Enable(Chip_Select_Address_out), .nA___nB(n2_to_4_decoder_1_na___nb),
    .A___nB(n2_to_4_decoder_1_a___nb), .nA___B(n2_to_4_decoder_1_na___b), .A___B(n2_to_4_decoder_1_a___b));
  or or_1 (or_1_out, in_2[7], in_2[6], in_2[5], in_2[4], in_2[3], in_2[2]);
  assign _8_Bit_Data_Bus = not_2_out ? in_1 : 8'bz;  // Controlled_Buffer controlled_buffer_1
  assign controlled_buffer_2_out = not_2_out ? _8_Bit_Data_Bus : 8'bz;  // Controlled_Buffer controlled_buffer_2
  _8_Bit_Memory_Cell u_8_bit_memory_cell_1 (
    .D0(controlled_buffer_2_out[0]), .D1(controlled_buffer_2_out[1]), .D2(controlled_buffer_2_out[2]),
    .D3(controlled_buffer_2_out[3]), .D4(controlled_buffer_2_out[4]), .D5(controlled_buffer_2_out[5]),
    .D6(controlled_buffer_2_out[6]), .D7(controlled_buffer_2_out[7]), .Enable(n2_to_4_decoder_1_na___nb),
    .Read_1___Write_0(in_3[1]), .Q0(n8_bit_memory_cell_1_q0), .Q1(n8_bit_memory_cell_1_q1),
    .Q2(n8_bit_memory_cell_1_q2), .Q3(n8_bit_memory_cell_1_q3), .Q4(n8_bit_memory_cell_1_q4),
    .Q5(n8_bit_memory_cell_1_q5), .Q6(n8_bit_memory_cell_1_q6), .Q7(n8_bit_memory_cell_1_q7));
  _8_Bit_Memory_Cell u_8_bit_memory_cell_2 (
    .D0(controlled_buffer_2_out[0]), .D1(controlled_buffer_2_out[1]), .D2(controlled_buffer_2_out[2]),
    .D3(controlled_buffer_2_out[3]), .D4(controlled_buffer_2_out[4]), .D5(controlled_buffer_2_out[5]),
    .D6(controlled_buffer_2_out[6]), .D7(controlled_buffer_2_out[7]), .Enable(n2_to_4_decoder_1_a___nb),
    .Read_1___Write_0(in_3[1]), .Q0(n8_bit_memory_cell_2_q0), .Q1(n8_bit_memory_cell_2_q1),
    .Q2(n8_bit_memory_cell_2_q2), .Q3(n8_bit_memory_cell_2_q3), .Q4(n8_bit_memory_cell_2_q4),
    .Q5(n8_bit_memory_cell_2_q5), .Q6(n8_bit_memory_cell_2_q6), .Q7(n8_bit_memory_cell_2_q7));
  _8_Bit_Memory_Cell u_8_bit_memory_cell_3 (
    .D0(controlled_buffer_2_out[0]), .D1(controlled_buffer_2_out[1]), .D2(controlled_buffer_2_out[2]),
    .D3(controlled_buffer_2_out[3]), .D4(controlled_buffer_2_out[4]), .D5(controlled_buffer_2_out[5]),
    .D6(controlled_buffer_2_out[6]), .D7(controlled_buffer_2_out[7]), .Enable(n2_to_4_decoder_1_na___b),
    .Read_1___Write_0(in_3[1]), .Q0(n8_bit_memory_cell_3_q0), .Q1(n8_bit_memory_cell_3_q1),
    .Q2(n8_bit_memory_cell_3_q2), .Q3(n8_bit_memory_cell_3_q3), .Q4(n8_bit_memory_cell_3_q4),
    .Q5(n8_bit_memory_cell_3_q5), .Q6(n8_bit_memory_cell_3_q6), .Q7(n8_bit_memory_cell_3_q7));
  _8_Bit_Memory_Cell u_8_bit_memory_cell_4 (
    .D0(controlled_buffer_2_out[0]), .D1(controlled_buffer_2_out[1]), .D2(controlled_buffer_2_out[2]),
    .D3(controlled_buffer_2_out[3]), .D4(controlled_buffer_2_out[4]), .D5(controlled_buffer_2_out[5]),
    .D6(controlled_buffer_2_out[6]), .D7(controlled_buffer_2_out[7]), .Enable(n2_to_4_decoder_1_a___b),
    .Read_1___Write_0(in_3[1]), .Q0(n8_bit_memory_cell_4_q0), .Q1(n8_bit_memory_cell_4_q1),
    .Q2(n8_bit_memory_cell_4_q2), .Q3(n8_bit_memory_cell_4_q3), .Q4(n8_bit_memory_cell_4_q4),
    .Q5(n8_bit_memory_cell_4_q5), .Q6(n8_bit_memory_cell_4_q6), .Q7(n8_bit_memory_cell_4_q7));
  not not_2 (not_2_out, and_1_out);
  or D7 (D0_out[7], n8_bit_memory_cell_4_q7, n8_bit_memory_cell_3_q7, n8_bit_memory_cell_2_q7, n8_bit_memory_cell_1_q7);
  or D5 (D0_out[5], n8_bit_memory_cell_4_q5, n8_bit_memory_cell_3_q5, n8_bit_memory_cell_2_q5, n8_bit_memory_cell_1_q5);
  or D6 (D0_out[6], n8_bit_memory_cell_4_q6, n8_bit_memory_cell_3_q6, n8_bit_memory_cell_2_q6, n8_bit_memory_cell_1_q6);
  or D4 (D0_out[4], n8_bit_memory_cell_4_q4, n8_bit_memory_cell_3_q4, n8_bit_memory_cell_2_q4, n8_bit_memory_cell_1_q4);
  or D3 (D0_out[3], n8_bit_memory_cell_4_q3, n8_bit_memory_cell_3_q3, n8_bit_memory_cell_2_q3, n8_bit_memory_cell_1_q3);
  assign _8_Bit_Data_Bus = and_1_out ? D0_out : 8'bz;  // Controlled_Buffer controlled_buffer_3
  or D1 (D0_out[1], n8_bit_memory_cell_4_q1, n8_bit_memory_cell_3_q1, n8_bit_memory_cell_2_q1, n8_bit_memory_cell_1_q1);
  or D2 (D0_out[2], n8_bit_memory_cell_4_q2, n8_bit_memory_cell_3_q2, n8_bit_memory_cell_2_q2, n8_bit_memory_cell_1_q2);
  or D0 (D0_out[0], n8_bit_memory_cell_4_q0, n8_bit_memory_cell_3_q0, n8_bit_memory_cell_2_q0, n8_bit_memory_cell_1_q0);

  assign _8_Bit_Address_Buss = in_2;
  assign Control_Bus = in_3;

  // Notes on the sheet:
  //   Control Bus Lines
  //   #0 Clock
  //   #1 Read(1) / Write (0)
  //   Cell Select Address
  //   Memory Cell Input
endmodule
